// Logisim project comp.circ as structural Verilog: 7 circuits, main circuit main
module main (
);

  wire A_In, A_Out, Addr_H_In, Addr_L_In, Addr_Shift, ALU_C_In, ALU_C_Out, and_2_out, and_3_out, and_4_out,
       B_In, B_Out, BF, C_Clear, C_Set, CF, CF_En, CLK, clock_1_out, CNT_En, Cnt_H_In, Cnt_H_Out, Cnt_L_In,
       Cnt_L_Out, D_Clear, d_ff_1_q, D_Set, decoder_2_out0, decoder_2_out1, decoder_2_out2, decoder_4_out0,
       DF, F_In, F_Out, First_Select, HLT, I_Clear, I_Set, IF, Inst_In, LCF, Mic_RST, NF_En, nor_1_out,
       nor_3_out, not_1_out, not_2_out, or_1_out, or_2_out, or_3_out, or_4_out, P_Cnt_Lo_carry, SP_In,
       V_Clear, VF_En, Write, X_In, X_Out, Y_In, Y_Out, ZF_En;
  wire [1:0] Addr_Out, Use_C_F;
  wire [1:1] d_ff_1_qn;
  wire [2:0] ALU_Out_Select, Data_Out_Select, Flag_Inst, Second_Select;
  wire [3:0] Micro_q, OP_Select;
  wire [3:1] Condition;
  wire [6:0] keyboard_1_data;
  wire [7:0] A_Val, Addr_H_Val, Addr_L_Val, ALU_Out, B_Val, controlled_buffer_6_out, Data, Inst_q,
       multiplexer_1_out, multiplexer_3_out, random_1_out, SP_Val, X_Val, Y_Val;
  wire [7:1] nz_1_z;
  wire [15:0] addrselecter_1_out_6, P_Cnt_Lo_q, pc_alu_1_out_5;
  wire [31:0] videocard_1_out_5, videocard_1_out_6, videocard_1_out_7, videocard_1_out_8, videocard_1_out_9,
       videocard_1_out_10, videocard_1_out_11, videocard_1_out_12, videocard_1_out_13, videocard_1_out_14,
       videocard_1_out_15, videocard_1_out_16, videocard_1_out_17, videocard_1_out_18, videocard_1_out_19,
       videocard_1_out_20, videocard_1_out_21, videocard_1_out_22, videocard_1_out_23, videocard_1_out_24,
       videocard_1_out_25, videocard_1_out_26, videocard_1_out_27, videocard_1_out_28, videocard_1_out_29,
       videocard_1_out_30, videocard_1_out_31, videocard_1_out_32, videocard_1_out_33, videocard_1_out_34,
       videocard_1_out_35, videocard_1_out_36;
  wire [31:31] rom_2_data;

  Clock clock_1 (.out(clock_1_out));
  D_Flip_Flop d_ff_1 (
    .clk(CLK), .D(d_ff_1_qn[1]), .Q(d_ff_1_q), .Qn(d_ff_1_qn[1]), .en(d_ff_1_qn[1]));  // open: preset, reset
  and and_1 (CLK, clock_1_out, ~HLT);  // AND_Gate
  nor nor_1 (nor_1_out, addrselecter_1_out_6[14], addrselecter_1_out_6[15]);
  Register Addr_Lo (.D(ALU_Out), .en(Addr_L_In), .Q(Addr_L_Val), .clk(CLK));  // open: clr
  Counter #(.width(4), .max('hf), .trigger("falling")) Micro (
    .Q(Micro_q), .clk(CLK), .clr(Mic_RST));  // open: load, D, count, carry
  Multiplexer #(.width(8), .enable("false")) multiplexer_1 (
    .in0(Data), .in1({8{1'b1}}), .out(multiplexer_1_out), .sel(d_ff_1_qn[1]));
  Register Inst (.D(multiplexer_1_out), .en(Inst_In), .Q(Inst_q), .clk(CLK));  // open: clr
  not not_1 (not_1_out, d_ff_1_qn[1]);
  not not_2 (not_2_out, Write);
  Register Addr_Hi (.D(ALU_Out), .en(Addr_H_In), .Q(Addr_H_Val), .clk(CLK));  // open: clr
  assign Inst_In = d_ff_1_qn[1] ? d_ff_1_qn[1] : 1'bz;  // Controlled_Buffer controlled_buffer_1
  assign Addr_Out = d_ff_1_qn[1] ? {2{d_ff_1_qn[1]}} : 2'bz;  // Controlled_Buffer controlled_buffer_2
  assign CNT_En = d_ff_1_qn[1] ? not_1_out : 1'bz;  // Controlled_Buffer controlled_buffer_3
  RAM #(.addrWidth(14)) ram_1 (
    .addr(addrselecter_1_out_6[13:0]), .data(Data), .sel(nor_1_out), .clk(CLK), .ld(not_2_out), .clr(1'b0));
  ROM #(.addrWidth(15)) rom_1 (.addr(addrselecter_1_out_6[14:0]), .data(Data), .sel(addrselecter_1_out_6[15]));
  // Probe on {Condition, CF, Inst_q, Micro_q}
  // Probe on Data
  // Probe on addrselecter_1_out_6
  nor nor_2 (HLT, Addr_Out[0], Addr_Out[1], Cnt_L_In, Cnt_H_In, CNT_En, Inst_In, First_Select, Second_Select[0], Second_Select[1], Second_Select[2], OP_Select[0], OP_Select[1], OP_Select[2], OP_Select[3], ALU_Out_Select[0], ALU_Out_Select[1], Data_Out_Select[0], Data_Out_Select[1], Data_Out_Select[2], Flag_Inst[0], Flag_Inst[1], Flag_Inst[2], Use_C_F[0], Use_C_F[1], CF_En, ZF_En, VF_En, NF_En, Addr_Shift, Mic_RST, rom_2_data[31], ALU_Out_Select[2]);
  PC_ALU pc_alu_1 (
    .Addr({Addr_H_Val, Addr_L_Val}), .PC(P_Cnt_Lo_q), .Shift(B_Val), .ShiftAddr(Addr_Shift),
    .out_5(pc_alu_1_out_5));
  ROM #(.addrWidth(16), .dataWidth(32)) rom_2 (
    .addr({Condition, CF, Inst_q, Micro_q}),
    .data({rom_2_data[31], Mic_RST, Addr_Shift, NF_En, VF_En, ZF_En, CF_En, Use_C_F, Flag_Inst, Data_Out_Select, ALU_Out_Select, OP_Select, Second_Select, First_Select, Inst_In, CNT_En, Cnt_H_In, Cnt_L_In, Addr_Out}),
    .sel(d_ff_1_q));
  nor nor_3 (nor_3_out, addrselecter_1_out_6[15], addrselecter_1_out_6[8], addrselecter_1_out_6[9], addrselecter_1_out_6[10], addrselecter_1_out_6[11]);
  Counter #(.trigger("falling")) P_Cnt_Lo (
    .load(Cnt_L_In), .D(pc_alu_1_out_5[7:0]), .count(CNT_En), .Q(P_Cnt_Lo_q[7:0]), .carry(P_Cnt_Lo_carry),
    .clk(CLK));  // open: clr
  and and_2 (and_2_out, nor_3_out, addrselecter_1_out_6[12], addrselecter_1_out_6[13], addrselecter_1_out_6[14]);
  Counter #(.trigger("falling")) P_Cnt_Hi (
    .load(Cnt_H_In), .D(pc_alu_1_out_5[15:8]), .count(and_3_out), .Q(P_Cnt_Lo_q[15:8]), .clk(CLK));  // open: carry, clr
  and and_3 (and_3_out, P_Cnt_Lo_carry, CNT_En);
  Decoder #(.select(3), .disabled(0), .enable("false")) decoder_1 (
    .out0(B_In), .out1(A_In), .out2(X_In), .out3(Y_In), .out4(SP_In), .out5(Addr_H_In), .out6(Addr_L_In),
    .out7(F_In), .sel(ALU_Out_Select));
  Decoder #(.select(2), .disabled(0)) decoder_2 (
    .out0(decoder_2_out0), .out1(decoder_2_out1), .out2(decoder_2_out2), .sel(addrselecter_1_out_6[1:0]),
    .en(and_2_out));  // open: out3
  assign Data = Cnt_L_Out ? P_Cnt_Lo_q[7:0] : 8'bz;  // Controlled_Buffer controlled_buffer_4
  AddrSelecter addrselecter_1 (
    .B(B_Val), .SP(SP_Val), .Addr({Addr_H_Val, Addr_L_Val}), .PC(P_Cnt_Lo_q), .Selecter(Addr_Out),
    .out_6(addrselecter_1_out_6));
  assign Data = Cnt_H_Out ? P_Cnt_Lo_q[15:8] : 8'bz;  // Controlled_Buffer controlled_buffer_5
  Decoder #(.select(3), .disabled(0), .enable("false")) decoder_3 (
    .out1(C_Clear), .out2(C_Set), .out3(I_Clear), .out4(I_Set), .out5(V_Clear), .out6(D_Clear), .out7(D_Set),
    .sel(Flag_Inst));  // open: out0
  and and_4 (and_4_out, CLK, decoder_2_out0);
  assign controlled_buffer_6_out = decoder_2_out0 ? Data : 8'bz;  // Controlled_Buffer controlled_buffer_6
  Keyboard keyboard_1 (.clk(CLK), .re(decoder_2_out1), .data(keyboard_1_data));  // open: clr, avail
  assign Data = decoder_2_out1 ? {1'b0, keyboard_1_data} : 8'bz;  // Controlled_Buffer controlled_buffer_7
  assign Data = decoder_2_out2 ? random_1_out : 8'bz;  // Controlled_Buffer controlled_buffer_8
  Random random_1 (.clk(CLK), .next(decoder_2_out2), .out(random_1_out));  // open: clr
  NZ nz_1 (.in_1(ALU_Out), .Z(nz_1_z[1]), .N(nz_1_z[7]));
  TTY tty_1 (
    .data(controlled_buffer_6_out[6:0]), .clk(and_4_out), .we(decoder_2_out0),
    .clr(controlled_buffer_6_out[7]));
  Decoder #(.select(3), .disabled(0), .enable("false")) decoder_4 (
    .out0(decoder_4_out0), .out1(A_Out), .out2(B_Out), .out3(Cnt_H_Out), .out4(Cnt_L_Out), .out5(X_Out),
    .out6(Y_Out), .out7(F_Out), .sel(Data_Out_Select));
  Multiplexer #(.select(2), .enable("false")) multiplexer_2 (
    .in0(1'b0), .in1(1'b1), .in2(LCF), .in3(CF), .out(ALU_C_In), .sel(Use_C_F));
  not not_3 (Write, decoder_4_out0);
  Multiplexer #(.width(8), .disabled(0), .enable("false")) multiplexer_3 (
    .in0({nz_1_z[7], 1'b0, ALU_C_Out, 3'b000, nz_1_z[1], ALU_C_Out}), .in1(ALU_Out), .out(multiplexer_3_out),
    .sel(F_In));
  Joystick joystick_1 ();  // open: x, y
  ALU alu_1 (
    .Data(Data), .A(A_Val), .X(X_Val), .Y(Y_Val), .SP(SP_Val), .AddrL(Addr_L_Val), .AddrH(Addr_H_Val),
    .B(B_Val), .C_In(ALU_C_In), .First_select(First_Select), .Second_select(Second_Select),
    .Op_select(OP_Select), .Q(ALU_Out), .C_Out(ALU_C_Out));
  D_Flip_Flop C (
    .clk(CLK), .D(multiplexer_3_out[0]), .Q(CF), .preset(C_Set), .en(or_1_out), .reset(C_Clear));  // open: Qn
  or or_1 (or_1_out, CF_En, F_In);
  D_Flip_Flop Z (.clk(CLK), .D(multiplexer_3_out[1]), .Q(Condition[1]), .en(or_2_out));  // open: Qn, preset, reset
  or or_2 (or_2_out, ZF_En, F_In);
  D_Flip_Flop I (.clk(CLK), .D(multiplexer_3_out[2]), .Q(IF), .preset(I_Set), .en(F_In), .reset(I_Clear));  // open: Qn
  D_Flip_Flop D (.clk(CLK), .D(multiplexer_3_out[3]), .Q(DF), .preset(D_Set), .en(F_In), .reset(D_Clear));  // open: Qn
  D_Flip_Flop B (.clk(CLK), .D(multiplexer_3_out[4]), .Q(BF), .en(F_In));  // open: Qn, preset, reset
  D_Flip_Flop Last_C (.clk(CLK), .D(multiplexer_3_out[5]), .Q(LCF), .en(1'b1));  // open: Qn, preset, reset
  D_Flip_Flop V (
    .clk(CLK), .D(multiplexer_3_out[6]), .Q(Condition[2]), .en(or_3_out), .reset(V_Clear));  // open: Qn, preset
  or or_3 (or_3_out, VF_En, F_In);
  D_Flip_Flop N (.clk(CLK), .D(multiplexer_3_out[7]), .Q(Condition[3]), .en(or_4_out));  // open: Qn, preset, reset
  or or_4 (or_4_out, NF_En, F_In);
  DotMatrix #(.matrixcols(32), .matrixrows(32), .persist(2200)) dotmatrix_1 (
    .col0(videocard_1_out_21), .col1(videocard_1_out_5), .col2(videocard_1_out_22), .col3(videocard_1_out_6),
    .col4(videocard_1_out_23), .col5(videocard_1_out_7), .col6(videocard_1_out_24), .col7(videocard_1_out_8),
    .col8(videocard_1_out_25), .col9(videocard_1_out_9), .col10(videocard_1_out_26),
    .col11(videocard_1_out_10), .col12(videocard_1_out_27), .col13(videocard_1_out_11),
    .col14(videocard_1_out_28), .col15(videocard_1_out_12), .col16(videocard_1_out_29),
    .col17(videocard_1_out_13), .col18(videocard_1_out_30), .col19(videocard_1_out_14),
    .col20(videocard_1_out_31), .col21(videocard_1_out_15), .col22(videocard_1_out_32),
    .col23(videocard_1_out_16), .col24(videocard_1_out_33), .col25(videocard_1_out_17),
    .col26(videocard_1_out_34), .col27(videocard_1_out_18), .col28(videocard_1_out_35),
    .col29(videocard_1_out_19), .col30(videocard_1_out_36), .col31(videocard_1_out_20));
  videocard videocard_1 (
    .Data(Data), .Addr(addrselecter_1_out_6), .Write(Write), .Clock(CLK), .out_21(videocard_1_out_21),
    .out_5(videocard_1_out_5), .out_22(videocard_1_out_22), .out_6(videocard_1_out_6),
    .out_23(videocard_1_out_23), .out_7(videocard_1_out_7), .out_24(videocard_1_out_24),
    .out_8(videocard_1_out_8), .out_25(videocard_1_out_25), .out_9(videocard_1_out_9),
    .out_26(videocard_1_out_26), .out_10(videocard_1_out_10), .out_27(videocard_1_out_27),
    .out_11(videocard_1_out_11), .out_28(videocard_1_out_28), .out_12(videocard_1_out_12),
    .out_29(videocard_1_out_29), .out_13(videocard_1_out_13), .out_30(videocard_1_out_30),
    .out_14(videocard_1_out_14), .out_31(videocard_1_out_31), .out_15(videocard_1_out_15),
    .out_32(videocard_1_out_32), .out_16(videocard_1_out_16), .out_33(videocard_1_out_33),
    .out_17(videocard_1_out_17), .out_34(videocard_1_out_34), .out_18(videocard_1_out_18),
    .out_35(videocard_1_out_35), .out_19(videocard_1_out_19), .out_36(videocard_1_out_36),
    .out_20(videocard_1_out_20));
  Register A (.D(ALU_Out), .en(A_In), .Q(A_Val), .clk(CLK));  // open: clr
  Register X (.D(ALU_Out), .en(X_In), .Q(X_Val), .clk(CLK));  // open: clr
  Register Y (.D(ALU_Out), .en(Y_In), .Q(Y_Val), .clk(CLK));  // open: clr
  Register SP (.D(ALU_Out), .en(SP_In), .Q(SP_Val), .clk(CLK));  // open: clr
  Register B_2 (.D(ALU_Out), .en(B_In), .Q(B_Val), .clk(CLK));  // open: clr
  assign Data = A_Out ? A_Val : 8'bz;  // Controlled_Buffer controlled_buffer_9
  assign Data = X_Out ? X_Val : 8'bz;  // Controlled_Buffer controlled_buffer_10
  assign Data = Y_Out ? Y_Val : 8'bz;  // Controlled_Buffer controlled_buffer_11
  assign Data = B_Out ? B_Val : 8'bz;  // Controlled_Buffer controlled_buffer_12
  assign Data = F_Out ? {Condition[3:2], 1'b1, BF, DF, IF, Condition[1], CF} : 8'bz;  // Controlled_Buffer controlled_buffer_13

  // Other names for the same wires on the sheet: Condition[0] = CF; ZF = Condition[1]; VF = Condition[2];
  //   NF = Condition[3]

  // Notes on the sheet:
  //   contents of rom_1 (hex, n*v repeats v):
  //   80 7f 86 0 84 1 a0 0 b1 0 f0 7 8d 0 70 c8 4c 8 80 60 ad 1 70 f0 fb 60 a2 0 20 14 80 8d 0 70 c9 8 d0
  //   4 ca 4c 1c 80 c9 a d0 5 a9 0 95 10 60 95 10 e8 4c 1c 80 86 10 84 11 8a 18 4*6a 29 e0 18 65 11 aa a5
  //   10 4a 4a 4a 18 69 78 a8 60 85 14 20 39 80 86 12 84 13 a5 14 a2 0 81 12 60 54 79 70 65 20 79 6f 75 72
  //   20 6e 61 6d 65 3a 20 0 48 65 6c 6c 6f 20 0 2c 20 6e 69 63 65 20 74 6f 20 6d 65 65 74 20 79 6f 75 21
  //   0 a2 63 a0 80 20 2 80 20 1a 80 a2 74 a0 80 20 2 80 a2 10 a0 0 20 2 80 a2 7b a0 80 20 2 80 20 14 80
  //   60 a9 0 85 6 a5 6 c9 20 f0 c aa a8 a9 1 20 53 80 e6 6 4c b6 80 a9 0 85 6 a5 6 c9 20 f0 11 aa a9 1f
  //   18 e5 6 a8 a9 1 20 53 80 e6 6 4c cc 80 20 14 80 60 3d 66 4c 24 1b 1a 19 18 17 16 15 14 13 3c 3b 3a
  //   34 33 32 5d 5c 52 51 50 4f 7e 7d 72 71 70 6f 6e 9f 9e 93 92 90 8f 8e 8d bf be b4 b3 b0 af ae ad ac
  //   df d5 d4 cf ce cd cc cb ff f6 f5 ef ed ec eb ea 1f 17 16 f c b a 9 3f 38 37 36 35 30 2f 2b 2a 29 28
  //   5f 59 58 56 55 54 51 50 4f 4a 49 48 47 7f 7e 7a 79 75 74 73 72 71 70 6f 69 68 67 66 9f 9e 9b 9a 94
  //   93 92 91 90 8f 88 87 86 85 be bd bc bb b4 b3 b2 b1 b0 a7 a6 a5 a4 dd dc d5 d4 d3 d2 d1 d0 c6 c5 c4
  //   c3 fd fc fb fa f6 f5 f4 f3 f2 f1 f0 ef e5 e4 e3 e2 1d 1c 1b 1a 19 18 17 16 15 14 13 10 f e 4 3 2 1
  //   3c 3b 3a 39 2f 2e 2d 23 22 21 20 5b 5a 59 58 4e 4d 4c 42 41 40 7a 79 78 77 6d 6c 6b 61 60 99 98 97
  //   96 8c 8b 8a b8 b7 b6 b5 ab aa a9 d7 d6 d5 d4 ca c9 c8 f6 f5 f4 f3 e9 e8 e7 15 14 13 12 8 7 6 34 33
  //   32 31 27 26 53 52 51 50 72 71 70 6f 91 90 8f 8e b0 af ae ad cf ce cd cc ee ed ec 3a 34 3f 3e 58 57
  //   56 55 54 53 52 51 50 4f 4e 4d 79 78 77 76 70 6f 6e 6d 6c 6b 6a 69 9a 99 98 8b 8a 89 88 87 86 ba b9
  //   a8 a7 a6 a5 a4 db da c9 c8 c7 c6 c5 c4 c3 fb fa e7 e6 e5 e4 e3 e2 e1 1b 5 4 3 2 1 0 3b 3a 38 37 36
  //   35 23 22 21 20 5b 5a 59 58 57 56 40 7a 79 78 64 63 60 9b 9a 84 83 82 81 80 bb ba a2 a1 a0 dd dc db
  //   c1 c0 fe fd fc fb e0 1f 1e 1d 1c 1b 0 3f 3e 3b 21 20 5b 5a 42 41 40 7b 7a 62 61 60 9a 99 87 86 80 bb
  //   ba b9 b8 b1 b0 af ae ad ac ab aa a9 a8 a7 a6 a0 db da d4 d3 d2 d1 d0 cf ce cd cc cb ca c1 c0 fb f9
  //   e2 e1 e0 1b 1a 19 18 3 2 1 3b 3a 39 38 25 24 23 5a 59 58 57 48 47 46 45 44 7a 79 78 75 74 73 72 71
  //   70 6b 6a 69 68 67 66 99 98 97 96 90 8f 8e 8d 8c 8b 8a 89 b8 b7 b6 b5 b4 b3 b2 b1 b0 af ae ad 49 95
  //   89 49 33 32 31 2e 2d 2a 29 56 55 53 52 51 4e 4d 4c 4a 49 48 76 75 74 72 71 6e 6d 6a 69 68 96 95 89
  //   87 86 85 ba b9 b8 b1 b0 ad ac a7 a6 a5 da d9 d8 d2 d1 d0 cd cc cb c6 c5 fa f9 f8 f5 f4 f3 f1 f0 ed
  //   ec ea e9 e8 e7 e6 e4 e3 e2 1b 15 14 13 a 9 8 7 6 5 4 3 2 3c 3b 3a 35 34 32 31 30 2f 2e 2d 2c 2b 29
  //   28 27 26 25 23 22 5c 5b 5a 58 57 56 53 52 51 50 4f 4e 4d 4c 4b 4a 49 48 47 46 45 42 41 78 77 76 74
  //   73 72 71 70 6f 6e 6d 6c 6b 6a 69 68 67 66 65 62 61 60 9d 9c 97 95 94 93 92 91 8c 8b 8a 89 88 86 82
  //   81 80 bf be bd bc bb b8 b5 b4 b3 b2 aa a9 a8 a5 df de dd dc db da d9 d8 d7 d5 d4 d3 ca c9 c8 c6 c5
  //   c4 ff fe fd fc fb fa f9 f8 f7 f5 f4 f3 ea e9 e8 e7 e6 e5 e4 e2 e1 e0 1f 1e 1d 1c 1b 1a 18 15 14 13 a
  //   9 8 7 2 1 0 3f 3e 3d 3c 3b 3a 35 34 33 2a 29 28 21 20 5f 5e 5d 5c 5b 59 58 57 55 54 53 52 4a 49 48
  //   46 45 44 7c 79 78 77 75 74 73 72 71 6b 6a 69 68 66 65 64 62 61 60 9b 98 94 93 92 91 90 8f 8e 8d 8c
  //   8b 8a 89 85 82 81 80 bc bb ba b7 b6 b5 b3 b2 b1 b0 af ae ad ac ab aa a8 a7 a6 a2 a1 dc db da d7 d6
  //   d5 d2 d1 d0 cf ce cd cc cb c8 c7 c6 c3 fb f7 f6 f5 ef ee e8 e7 e6 e4 e3 e2 1a 19 18 13 12 f e b a 9
  //   4 3 2 3a 39 38 34 33 32 2f 2e 2d 2b 2a 29 26 5a 59 58 53 52 4f 4e 4b 4a 47 46 45 77 76 75 67 66 65
  //   97 96 95 92 91 8e 8d 8a 89 88 b6 b5 b3 b2 b1 af ae ad aa a9 a8 d3 d2 d1 cf ce cd ca c9 0 58 56 0 6c
  //   6b 6a 69 68 67 66 65 64 63 62 61 60 99 98 97 96 95 94 93 92 91 90 8f 8e 8d 8c 8b 8a 81 80 bb ba b9
  //   b8 b7 b6 b5 b4 b3 b2 b1 b0 af ae ad ac ab aa a1 a0 dd dc db da d9 d8 d7 d6 cc cb ca c9 c8 c7 c6 c5
  //   c4 c3 c2 c1 c0 ff fe fd fc fa f9 f8 f7 f6 ee ed ec eb ea e1 e0 1f 1e 1d 1c 1a 18 17 16 e d c b a 1 0
  //   3d 3c 3b 3a 39 38 37 2c 2b 2a 29 28 27 26 25 24 23 22 21 20 5b 5a 59 58 57 56 55 54 53 52 51 50 4f
  //   4e 4d 4c 4b 4a 41 40 79 78 77 76 75 74 73 72 71 70 6f 6e 6d 6c 6b 6a 61 60 8c 8b 8a 89 88 87 86 85
  //   84 83 82 81 80 4a 70 5c 42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
  //   contents of rom_2 (hex, n*v repeats v):
  //   16*0 30 14000 18150 41 818280 14041 18380 140048c1 40000000 55*0 30 14000 18050 140048c1 40000000
  //   11*0 30 14000 18050 16001441 40001 40000000 26*0 30 e0003 810600 40000000 12*0 30 140048d0 40000000
  //   13*0 30 16005400 40000000 45*0 30 18050 14050 140048c1 40000000 11*0 30 18050 14050 16001441 40001
  //   40000000 26*0 30 50 2000038c 40000000 12*0 30 14000 18050 41 818280 14041 18380 1a400 1014300
  //   140048c1 40000000 53*0 30 14000 18150 140048c1 40000000 11*0 30 14000 18150 16001441 40001 40000000
  //   26*0 30 100000 40000000 13*0 30 181d0 1014050 140048c1 40000000 59*0 30 18150 1014050 140048c1
  //   40000000 11*0 30 18150 1014050 16001441 40001 40000000 26*0 30 18050 14040 60003 810600 80003 810600
  //   c 40000000 7*0 30 14000 18150 41 818280 14041 18380 14004cc1 40000000 39*0 30 14000 18050 4000cc1
  //   40000000 11*0 30 14000 18050 14004cc1 40000000 11*0 30 14000 18050 17801c41 40001 40000000 26*0 30
  //   810200 1c043 40000000 12*0 30 14004cd0 40000000 13*0 30 17805c00 40000000 29*0 30 18050 14050
  //   4000cc1 40000000 11*0 30 18050 14050 14004cc1 40000000 11*0 30 18050 14050 17801c41 40001 40000000
  //   26*0 30 10 40000000 13*0 30 14000 18050 41 818280 14041 18380 1a400 1014300 14004cc1 40000000 53*0
  //   30 14000 18150 14004cc1 40000000 11*0 30 14000 18150 17801c41 40001 40000000 26*0 30 200000 40000000
  //   13*0 30 181d0 1014050 14004cc1 40000000 59*0 30 18150 1014050 14004cc1 40000000 11*0 30 18150
  //   1014050 17801c41 40001 40000000 42*0 30 14000 18150 41 818280 14041 18380 140050c1 40000000 55*0 30
  //   14000 18050 140050c1 40000000 11*0 30 14000 18050 16001841 40001 40000000 26*0 30 20003 810600
  //   40000000 12*0 30 140050d0 40000000 13*0 30 16005800 40000000 29*0 30 18050 14050 c 40000000 11*0 30
  //   18050 14050 140050c1 40000000 11*0 30 18050 14050 16001841 40001 40000000 26*0 30 50 2000038c
  //   40000000 12*0 30 14000 18050 41 818280 14041 18380 1a400 1014300 140050c1 40000000 53*0 30 14000
  //   18150 140050c1 40000000 11*0 30 14000 18150 16001841 40001 40000000 26*0 30 300000 40000000 13*0 30
  //   181d0 1014050 140050c1 40000000 59*0 30 18150 1014050 140050c1 40000000 11*0 30 18150 1014050
  //   16001841 40001 40000000 26*0 30 810200 18043 810200 14043 c 10 40000000 8*0 30 14000 18150 41 818280
  //   14041 18380 1f8040c1 40000000 55*0 30 14000 18050 1f8040c1 40000000 11*0 30 14000 18050 17802041
  //   40001 40000000 26*0 30 810200 4043 40000000 12*0 30 1f8040d0 40000000 13*0 30 17806000 40000000 29*0
  //   30 18050 14050 41 818280 1014300 14041 18380 c 40000000 6*0 30 18050 14050 1f8040c1 40000000 11*0 30
  //   18050 14050 17802041 40001 40000000 26*0 30 10 40000000 13*0 30 14000 18050 41 818280 14041 18380
  //   1a400 1014300 1f8040c1 40000000 53*0 30 14000 18150 1f8040c1 40000000 11*0 30 14000 18150 17802041
  //   40001 40000000 26*0 30 400000 40000000 13*0 30 181d0 1014050 1f8040c1 40000000 59*0 30 18150 1014050
  //   1f8040c1 40000000 11*0 30 18150 1014050 17802041 40001 40000000 42*0 30 14000 18150 41 818280 14041
  //   18380 20001 40000000 39*0 30 14000 18050 c0001 40000000 11*0 30 14000 18050 20001 40000000 11*0 30
  //   14000 18050 a0001 40000000 27*0 30 1480c580 40000000 29*0 30 14004100 40000000 29*0 30 18050 14050
  //   c0001 40000000 11*0 30 18050 14050 20001 40000000 11*0 30 18050 14050 a0001 40000000 27*0 30 50
  //   2000038c 40000000 12*0 30 14000 18050 41 818280 14041 18380 1a400 1014300 20001 40000000 37*0 30
  //   14000 18150 c0001 40000000 11*0 30 14000 18150 20001 40000000 11*0 30 14000 181d0 a0001 40000000
  //   27*0 30 14004180 40000000 13*0 30 181d0 1014050 20001 40000000 11*0 30 a0003 810600 40000000 44*0 30
  //   18150 1014050 20001 40000000 43*0 30 1400c050 40000000 13*0 30 14000 18150 41 818280 14041 18380
  //   14004041 40000000 7*0 30 14008050 40000000 29*0 30 14000 18050 1400c041 40000000 11*0 30 14000 18050
  //   14004041 40000000 11*0 30 14000 18050 14008041 40000000 27*0 30 1400c080 40000000 13*0 30 14004050
  //   40000000 13*0 30 14008080 40000000 29*0 30 18050 14050 1400c041 40000000 11*0 30 18050 14050
  //   14004041 40000000 11*0 30 18050 14050 14008041 40000000 27*0 30 10 40000000 13*0 30 14000 18050 41
  //   818280 14041 18380 1a400 1014300 14004041 40000000 37*0 30 14000 18150 14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
endmodule

module Monitor_PoC (
  input  [3:0] in_1,
  input  in_2
);

  wire and_1_out, and_2_out, button_1_out, clock_1_out, nor_1_out, ram_1_data;
  wire [1:0] register_1_q;
  wire [3:0] counter_1_q, demultiplexer_1_out0, demultiplexer_1_out1, demultiplexer_1_out2,
       demultiplexer_1_out3, multiplexer_1_out, shift_register_1_q3;

  Button button_1 (.out(button_1_out));
  Clock clock_1 (.out(clock_1_out));
  and and_1 (and_1_out, ~button_1_out, clock_1_out);  // AND_Gate
  Counter #(.width(4), .max('hf)) counter_1 (.Q(counter_1_q), .clk(and_1_out));  // open: load, D, count, carry, clr
  Multiplexer #(.width(4), .enable("false")) multiplexer_1 (
    .in0(counter_1_q), .in1(in_1), .out(multiplexer_1_out), .sel(button_1_out));
  and and_2 (and_2_out, button_1_out, clock_1_out);
  nor nor_1 (nor_1_out, counter_1_q[0], counter_1_q[1], and_1_out);
  RAM #(.addrWidth(4), .dataWidth(1), .bus("separate")) ram_1 (
    .addr(multiplexer_1_out), .din(in_2), .data(ram_1_data), .str(button_1_out), .clk(and_2_out));  // open: sel, ld, clr
  Register #(.width(2)) register_1 (
    .D(counter_1_q[3:2]), .en(nor_1_out), .Q(register_1_q), .clk(and_1_out));  // open: clr
  Shift_Register #(.length(4)) shift_register_1 (
    .shift(1'b1), .in(ram_1_data), .clk(and_1_out), .q0(shift_register_1_q3[3]), .q1(shift_register_1_q3[2]),
    .q2(shift_register_1_q3[1]), .q3(shift_register_1_q3[0]));  // open: out, load, clr, d0, d1, d2, d3
  DotMatrix #(.matrixcols(4), .matrixrows(4), .persist(40)) dotmatrix_1 (
    .col0(demultiplexer_1_out0), .col1(demultiplexer_1_out1), .col2(demultiplexer_1_out2),
    .col3(demultiplexer_1_out3));
  Demultiplexer #(.select(2), .width(4), .disabled(0)) demultiplexer_1 (
    .out0(demultiplexer_1_out0), .out1(demultiplexer_1_out1), .out2(demultiplexer_1_out2),
    .out3(demultiplexer_1_out3), .in(shift_register_1_q3), .sel(register_1_q), .en(nor_1_out));
endmodule

module NZ (
  input  [7:0] in_1,
  output Z,
  output N
);

  nor nor_1 (Z, in_1[3], in_1[0], in_1[1], in_1[2], in_1[4], in_1[5], in_1[6], in_1[7]);

  assign N = in_1[7];
endmodule

module ALU (
  input  C_In,
  input  [7:0] Data,
  input  [7:0] A,
  input  [7:0] X,
  input  [7:0] Y,
  input  [7:0] SP,
  input  [7:0] AddrL,
  input  [7:0] AddrH,
  input  [7:0] B,
  input  First_select,
  input  [2:0] Second_select,
  input  [3:0] Op_select,
  output [7:0] Q,
  output C_Out
);

  wire adder_1_cout, adder_2_cout, subtractor_1_bout;
  wire [7:0] adder_1_out, adder_2_out, and_1_out, multiplexer_1_out, multiplexer_2_out, multiplexer_3_out,
       or_1_out, subtractor_1_out, xor_1_out;

  Multiplexer #(.width(8), .enable("false")) multiplexer_1 (
    .in0({8{1'b0}}), .in1(Data), .out(multiplexer_1_out), .sel(First_select));
  Multiplexer #(.width(8), .enable("false")) multiplexer_2 (
    .in0(A), .in1(Data), .out(multiplexer_2_out), .sel(First_select));
  Multiplexer #(.select(3), .width(8), .enable("false")) multiplexer_3 (
    .in0({8{1'b0}}), .in1(A), .in2(X), .in3(Y), .in4(SP), .in5(AddrL), .in6(AddrH), .in7(B),
    .out(multiplexer_3_out), .sel(Second_select));
  Adder adder_1 (.a(multiplexer_1_out), .b(multiplexer_3_out), .out(adder_1_out), .cin(C_In), .cout(adder_1_cout));
  Subtractor subtractor_1 (
    .a(multiplexer_3_out), .b(multiplexer_1_out), .out(subtractor_1_out), .bin(C_In), .bout(subtractor_1_bout));
  assign or_1_out = multiplexer_1_out | multiplexer_3_out;  // OR_Gate or_1, 8 bits wide
  assign and_1_out = multiplexer_1_out & multiplexer_3_out;  // AND_Gate and_1, 8 bits wide
  assign xor_1_out = multiplexer_1_out ^ multiplexer_3_out;  // XOR_Gate xor_1, 8 bits wide
  Adder adder_2 (.a(AddrL), .b(Y), .out(adder_2_out), .cin(1'b0), .cout(adder_2_cout));
  Multiplexer #(.select(4), .width(8), .enable("false")) multiplexer_4 (
    .in0(adder_1_out), .in1(subtractor_1_out), .in2(or_1_out), .in3(and_1_out), .in4(xor_1_out),
    .in5({multiplexer_2_out[6:0], 1'b0}), .in6({1'b0, multiplexer_2_out[7:1]}),
    .in7({multiplexer_2_out[6:0], C_In}), .in8({C_In, multiplexer_2_out[7:1]}), .in9(adder_2_out), .out(Q),
    .sel(Op_select));  // open: in10, in11, in12, in13, in14, in15
  Multiplexer #(.select(4), .enable("false")) multiplexer_5 (
    .in0(adder_1_cout), .in1(subtractor_1_bout), .in2(1'b0), .in3(1'b0), .in4(1'b0),
    .in5(multiplexer_2_out[7]), .in6(multiplexer_2_out[0]), .in7(multiplexer_2_out[7]),
    .in8(multiplexer_2_out[0]), .in9(adder_2_cout), .out(C_Out), .sel(Op_select));  // open: in10, in11, in12, in13, in14, in15
endmodule

module PC_ALU (
  input  [15:0] Addr,
  input  [15:0] PC,
  input  [7:0] Shift,
  input  ShiftAddr,
  output [15:0] out_5
);

  wire [7:0] negator_1_out;
  wire [15:0] adder_1_out, bit_extender_1_out, bit_extender_2_out, multiplexer_1_out, subtractor_1_out;

  Negator negator_1 (.in(Shift), .out(negator_1_out));
  Adder #(.width(16)) adder_1 (.a(PC), .b(bit_extender_1_out), .out(adder_1_out));  // open: cin, cout
  assign bit_extender_1_out = {{8{1'b0}}, Shift};  // Bit_Extender bit_extender_1
  Subtractor #(.width(16)) subtractor_1 (.a(PC), .b(bit_extender_2_out), .out(subtractor_1_out));  // open: bin, bout
  assign bit_extender_2_out = {{8{1'b0}}, negator_1_out};  // Bit_Extender bit_extender_2
  Multiplexer #(.width(16), .enable("false")) multiplexer_1 (
    .in0(adder_1_out), .in1(subtractor_1_out), .out(multiplexer_1_out), .sel(Shift[7]));
  Multiplexer #(.width(16), .enable("false")) multiplexer_2 (
    .in0(Addr), .in1(multiplexer_1_out), .out(out_5), .sel(ShiftAddr));
endmodule

module AddrSelecter (
  input  [7:0] B,
  input  [7:0] SP,
  input  [15:0] Addr,
  input  [15:0] PC,
  input  [1:0] Selecter,
  output [15:0] out_6
);

  Multiplexer #(.select(2), .width(16), .enable("false")) multiplexer_1 (
    .in0(PC), .in1(Addr), .in2({{8{1'b0}}, B}), .in3({8'h1, SP}), .out(out_6), .sel(Selecter));
endmodule

module videocard (
  input  [7:0] Data,
  input  [15:0] Addr,
  input  Write,
  input  Clock,
  output [31:0] out_5,
  output [31:0] out_6,
  output [31:0] out_7,
  output [31:0] out_8,
  output [31:0] out_9,
  output [31:0] out_10,
  output [31:0] out_11,
  output [31:0] out_12,
  output [31:0] out_13,
  output [31:0] out_14,
  output [31:0] out_15,
  output [31:0] out_16,
  output [31:0] out_17,
  output [31:0] out_18,
  output [31:0] out_19,
  output [31:0] out_20,
  output [31:0] out_21,
  output [31:0] out_22,
  output [31:0] out_23,
  output [31:0] out_24,
  output [31:0] out_25,
  output [31:0] out_26,
  output [31:0] out_27,
  output [31:0] out_28,
  output [31:0] out_29,
  output [31:0] out_30,
  output [31:0] out_31,
  output [31:0] out_32,
  output [31:0] out_33,
  output [31:0] out_34,
  output [31:0] out_35,
  output [31:0] out_36
);

  wire and_1_out, and_2_out, and_3_out, and_4_out, and_5_out, nor_1_out, ram_1_data;
  wire [4:0] register_1_q;
  wire [9:0] counter_1_q, multiplexer_1_out;
  wire [31:0] shift_register_1_q31;

  and and_1 (and_1_out, Addr[11], Addr[12], Addr[13], Addr[14], ~Addr[15], Write);  // AND_Gate
  and and_2 (and_2_out, ~Addr[10], and_1_out);  // AND_Gate
  and and_3 (and_3_out, Addr[10], and_1_out);
  and and_4 (and_4_out, ~and_2_out, Clock);  // AND_Gate
  Counter #(.width(10), .max('h3ff)) counter_1 (.Q(counter_1_q), .clk(and_4_out));  // open: load, D, count, carry, clr
  Multiplexer #(.width(10), .enable("false")) multiplexer_1 (
    .in0(counter_1_q), .in1(Addr[9:0]), .out(multiplexer_1_out), .sel(and_2_out));
  nor nor_1 (nor_1_out, and_4_out, counter_1_q[1], counter_1_q[0], counter_1_q[2], counter_1_q[3], counter_1_q[4]);
  and and_5 (and_5_out, and_2_out, Clock);
  RAM #(.addrWidth(10), .dataWidth(1), .bus("separate")) ram_1 (
    .addr(multiplexer_1_out), .din(Data[0]), .data(ram_1_data), .str(and_2_out), .clk(and_5_out),
    .clr(and_3_out));  // open: sel, ld
  Register #(.width(5)) register_1 (
    .D(counter_1_q[9:5]), .en(nor_1_out), .Q(register_1_q), .clk(and_4_out));  // open: clr
  Shift_Register #(.length(32)) shift_register_1 (
    .shift(1'b1), .in(ram_1_data), .clk(and_4_out), .q0(shift_register_1_q31[31]),
    .q1(shift_register_1_q31[30]), .q2(shift_register_1_q31[29]), .q3(shift_register_1_q31[28]),
    .q4(shift_register_1_q31[27]), .q5(shift_register_1_q31[26]), .q6(shift_register_1_q31[25]),
    .q7(shift_register_1_q31[24]), .q8(shift_register_1_q31[23]), .q9(shift_register_1_q31[22]),
    .q10(shift_register_1_q31[21]), .q11(shift_register_1_q31[20]), .q12(shift_register_1_q31[19]),
    .q13(shift_register_1_q31[18]), .q14(shift_register_1_q31[17]), .q15(shift_register_1_q31[16]),
    .q16(shift_register_1_q31[15]), .q17(shift_register_1_q31[14]), .q18(shift_register_1_q31[13]),
    .q19(shift_register_1_q31[12]), .q20(shift_register_1_q31[11]), .q21(shift_register_1_q31[10]),
    .q22(shift_register_1_q31[9]), .q23(shift_register_1_q31[8]), .q24(shift_register_1_q31[7]),
    .q25(shift_register_1_q31[6]), .q26(shift_register_1_q31[5]), .q27(shift_register_1_q31[4]),
    .q28(shift_register_1_q31[3]), .q29(shift_register_1_q31[2]), .q30(shift_register_1_q31[1]),
    .q31(shift_register_1_q31[0]));  // open: out, load, clr, d0, d1, d2, d3, d4, d5, d6, d7, d8, d9, d10, d11, d12, d13, d14, d15, d16, d17, d18, d19, d20, d21, d22, d23, d24, d25, d26, d27, d28, d29, d30, d31
  Demultiplexer #(.select(5), .width(32), .disabled(0)) demultiplexer_1 (
    .out0(out_21), .out1(out_5), .out2(out_22), .out3(out_6), .out4(out_23), .out5(out_7), .out6(out_24),
    .out7(out_8), .out8(out_25), .out9(out_9), .out10(out_26), .out11(out_10), .out12(out_27),
    .out13(out_11), .out14(out_28), .out15(out_12), .out16(out_29), .out17(out_13), .out18(out_30),
    .out19(out_14), .out20(out_31), .out21(out_15), .out22(out_32), .out23(out_16), .out24(out_33),
    .out25(out_17), .out26(out_34), .out27(out_18), .out28(out_35), .out29(out_19), .out30(out_36),
    .out31(out_20), .in(shift_register_1_q31), .sel(register_1_q), .en(nor_1_out));
endmodule
